// Logisim project BCD_D.circ as structural Verilog
module BCD_b (
  input  A,
  input  B,
  input  C,
  input  D,
  output b_2
);

  wire nand_1_out, nand_2_out, nand_3_out, nand_4_out, nand_5_out, nand_6_out, nand_7_out, nand_8_out,
       nand_9_out, nor_1_out, nor_2_out, nor_3_out, nor_4_out, not_1_out, not_2_out, not_3_out, not_4_out,
       not_5_out, not_6_out;

  nor nor_1 (nor_1_out, A, C);
  nor nor_2 (nor_2_out, A, B);
  nand nand_1 (nand_1_out, D, D);
  not not_1 (not_1_out, A);
  not not_2 (not_2_out, C);
  not not_3 (not_3_out, nor_2_out);
  nand nand_2 (nand_2_out, nor_1_out, nand_1_out);
  nand nand_3 (nand_3_out, not_1_out, C);
  nand nand_4 (nand_4_out, A, not_2_out);
  nand nand_5 (nand_5_out, not_3_out, nand_2_out);
  nor nor_3 (nor_3_out, B, D);
  not not_4 (not_4_out, nand_3_out);
  not not_5 (not_5_out, nand_4_out);
  nand nand_6 (nand_6_out, not_4_out, D);
  nand nand_7 (nand_7_out, not_5_out, D);
  nor nor_4 (nor_4_out, nand_5_out, nor_3_out);
  nand nand_8 (nand_8_out, nand_6_out, nand_7_out);
  not not_6 (not_6_out, nand_8_out);
  nand nand_9 (nand_9_out, nor_4_out, not_6_out);
  not not_7 (b_2, nand_9_out);
endmodule
