// Logisim project BCD_E_more_than_2_inputs.circ as structural Verilog
module BCD_E_more_than_2_inputs (
  input  A,
  input  B,
  input  C,
  input  D,
  output E
);

  wire nand_1_out, nand_2_out, nand_3_out, not_1_out, not_2_out, not_3_out, not_4_out, not_5_out;

  not not_1 (not_1_out, A);
  not not_2 (not_2_out, B);
  not not_3 (not_3_out, C);
  not not_4 (not_4_out, A);
  not not_5 (not_5_out, C);
  nand nand_1 (nand_1_out, not_1_out, D);
  nand nand_2 (nand_2_out, not_2_out, not_3_out, D);
  nand nand_3 (nand_3_out, not_4_out, B, not_5_out);
  nand nand_4 (E, nand_1_out, nand_2_out, nand_3_out);
endmodule
