// Logisim project BCD_Main.circ as structural Verilog: 1 circuit, main circuit main
module main (
  input  in_1,
  input  in_2,
  input  in_3,
  input  in_4
);

  wire bcd_a_1_a_2, bcd_b_1_b_2, bcd_c2_1_c_2, bcd_c2_2_f, bcd_d_1_d_2, bcd_e_more_than_2_inputs_1_e,
       bcd_g_1_g;

  BCD_a bcd_a_1 (.A(in_1), .B(in_2), .C(in_3), .D(in_4), .a_2(bcd_a_1_a_2));
  BCD_b bcd_b_1 (.A(in_1), .B(in_2), .C(in_3), .D(in_4), .b_2(bcd_b_1_b_2));
  BCD_c2 bcd_c2_1 (.A(in_1), .B(in_2), .C(in_3), .D(in_4), .C_2(bcd_c2_1_c_2));
  BCD_d bcd_d_1 (.A(in_1), .B(in_2), .C(in_3), .D(in_4), .d_2(bcd_d_1_d_2));
  BCD_E_more_than_2_inputs bcd_e_more_than_2_inputs_1 (
    .A(in_1), .B(in_2), .C(in_3), .D(in_4), .E(bcd_e_more_than_2_inputs_1_e));
  BCD_c2 bcd_c2_2 (.A(in_1), .B(in_2), .C(in_3), .D(in_4), .F(bcd_c2_2_f));
  BCD_g bcd_g_1 (.A(in_1), .B(in_2), .C(in_3), .D(in_4), .g(bcd_g_1_g));
  _7_Segment_Display #(.active("false")) u_7_segment_display_1 (
    .g(bcd_g_1_g), .f(bcd_c2_2_f), .a(bcd_a_1_a_2), .b(bcd_b_1_b_2), .e(bcd_e_more_than_2_inputs_1_e),
    .d(bcd_d_1_d_2), .c(bcd_c2_1_c_2));  // open: dp
endmodule
