// Logisim project BCD_b.circ as structural Verilog: 1 circuit, main circuit BCD_b
module BCD_b (
  input  A,
  input  B,
  input  C,
  input  D,
  output b_2
);

  wire nand_1_out, nand_2_out, nand_3_out, nand_4_out, not_1_out, not_2_out, not_3_out, not_4_out;

  not not_1 (not_1_out, A);
  not not_2 (not_2_out, C);
  not not_3 (not_3_out, D);
  not not_4 (not_4_out, D);
  nand nand_1 (nand_1_out, not_1_out, B, not_2_out, D);
  nand nand_2 (nand_2_out, B, C, not_3_out);
  nand nand_3 (nand_3_out, A, C, D);
  nand nand_4 (nand_4_out, A, B, not_4_out);
  nand nand_5 (b_2, nand_1_out, nand_2_out, nand_3_out, nand_4_out);
endmodule
