// Logisim project BCD_c.circ as structural Verilog
module BCD_c (
  input  A,
  input  B,
  input  C,
  input  D,
  output c_2
);

  wire nand_1_out, nand_2_out, nand_3_out, nand_4_out, nand_5_out, nand_6_out, nand_7_out, nor_1_out,
       not_1_out, not_2_out, not_3_out, not_4_out, not_5_out;

  not not_1 (not_1_out, D);
  nor nor_1 (nor_1_out, A, B);
  nand nand_1 (nand_1_out, C, not_1_out);
  nand nand_2 (nand_2_out, A, B);
  not not_2 (not_2_out, nand_1_out);
  not not_3 (not_3_out, nand_2_out);
  nand nand_3 (nand_3_out, nor_1_out, not_2_out);
  nand nand_4 (nand_4_out, not_3_out, not_1_out);
  nand nand_5 (nand_5_out, A, B);
  nand nand_6 (nand_6_out, nand_3_out, nand_4_out);
  not not_4 (not_4_out, nand_5_out);
  not not_5 (not_5_out, nand_6_out);
  nand nand_7 (nand_7_out, not_4_out, C);
  nand nand_8 (c_2, not_5_out, nand_7_out);
endmodule
