// Logisim project BCD_d.circ as structural Verilog: 1 circuit, main circuit BCD_d
module BCD_d (
  input  A,
  input  B,
  input  C,
  input  D,
  output d_2
);

  wire nand_1_out, nand_2_out, nand_3_out, nand_4_out, not_1_out, not_2_out, not_3_out, not_4_out, not_5_out,
       not_6_out, not_7_out;

  not not_1 (not_1_out, B);
  not not_2 (not_2_out, C);
  not not_3 (not_3_out, A);
  not not_4 (not_4_out, C);
  not not_5 (not_5_out, D);
  not not_6 (not_6_out, B);
  not not_7 (not_7_out, D);
  nand nand_1 (nand_1_out, not_1_out, not_2_out, D);
  nand nand_2 (nand_2_out, not_3_out, B, not_4_out, not_5_out);
  nand nand_3 (nand_3_out, B, C, D);
  nand nand_4 (nand_4_out, A, not_6_out, C, not_7_out);
  nand nand_5 (d_2, nand_1_out, nand_2_out, nand_3_out, nand_4_out);
endmodule
