// Logisim project BCD_f.circ as structural Verilog: 1 circuit, main circuit BCD_f
module BCD_f (
  input  A,
  input  B,
  input  C,
  input  D,
  output f
);

  wire nand_1_out, nand_2_out, nand_3_out, nand_4_out, not_1_out, not_2_out, not_3_out;

  not not_1 (not_1_out, A);
  not not_2 (not_2_out, B);
  not not_3 (not_3_out, C);
  nand nand_1 (nand_1_out, not_1_out, not_2_out, D);
  nand nand_2 (nand_2_out, not_1_out, not_2_out, C);
  nand nand_3 (nand_3_out, not_1_out, C, D);
  nand nand_4 (nand_4_out, A, B, not_3_out, D);
  nand nand_5 (f, nand_1_out, nand_2_out, nand_3_out, nand_4_out);
endmodule
